// Logisim project PROJECT.circ as structural Verilog
module Full_Adder (
  input  A,
  input  B,
  input  C,
  output S,
  output C_2
);

  wire half_adder_1_c, half_adder_1_s, half_adder_2_c;

  Half_Adder half_adder_1 (.A(A), .B(B), .S(half_adder_1_s), .C(half_adder_1_c));
  Half_Adder half_adder_2 (.A(half_adder_1_s), .B(C), .S(S), .C(half_adder_2_c));
  or OR (C_2, half_adder_2_c, half_adder_1_c);
endmodule

module Half_Adder (
  input  A,
  input  B,
  output S,
  output C
);

  xor XOR (S, A, B);
  and AND (C, A, B);
endmodule

module _2_s_Compliment (
  input  [4:0] In,
  output [4:0] Out
);

  wire half_adder_1_c, half_adder_2_c, half_adder_3_c, half_adder_4_c, not_1_out, not_2_out, not_3_out,
       not_4_out, not_5_out;

  not not_1 (not_1_out, In[0]);
  not not_2 (not_2_out, In[1]);
  not not_3 (not_3_out, In[2]);
  not not_4 (not_4_out, In[3]);
  not not_5 (not_5_out, In[4]);
  Half_Adder half_adder_1 (.A(not_1_out), .B(1'b1), .S(Out[0]), .C(half_adder_1_c));
  Half_Adder half_adder_2 (.A(not_2_out), .B(half_adder_1_c), .S(Out[1]), .C(half_adder_2_c));
  Half_Adder half_adder_3 (.A(not_3_out), .B(half_adder_2_c), .S(Out[2]), .C(half_adder_3_c));
  Half_Adder half_adder_4 (.A(not_4_out), .B(half_adder_3_c), .S(Out[3]), .C(half_adder_4_c));
  Half_Adder half_adder_5 (.A(not_5_out), .B(half_adder_4_c), .S(Out[4]));  // open: C

  // Notes on the sheet:
  //   1 to get 2's compliment and 0 to get 1's compliment
endmodule

// Subtractor
module _5_bit_Subtractor (
  input  B4,
  input  A4,
  input  B3,
  input  A3,
  input  B2,
  input  A2,
  input  B1,
  input  A1,
  input  B0,
  input  A0,
  output C,
  output S4,
  output S3,
  output S2,
  output S1,
  output S0
);

  wire full_adder_2_c_2, full_adder_3_c_2, full_adder_4_c_2, full_adder_5_c_2, xor_1_out, xor_2_out,
       xor_3_out, xor_4_out, xor_5_out;

  xor xor_1 (xor_1_out, B4, 1'b1);
  Full_Adder full_adder_1 (.A(A4), .B(xor_1_out), .C(full_adder_2_c_2), .S(S4), .C_2(C));
  xor xor_2 (xor_2_out, B3, 1'b1);
  Full_Adder full_adder_2 (.A(A3), .B(xor_2_out), .C(full_adder_3_c_2), .S(S3), .C_2(full_adder_2_c_2));
  xor xor_3 (xor_3_out, B2, 1'b1);
  Full_Adder full_adder_3 (.A(A2), .B(xor_3_out), .C(full_adder_4_c_2), .S(S2), .C_2(full_adder_3_c_2));
  xor xor_4 (xor_4_out, B1, 1'b1);
  Full_Adder full_adder_4 (.A(A1), .B(xor_4_out), .C(full_adder_5_c_2), .S(S1), .C_2(full_adder_4_c_2));
  xor xor_5 (xor_5_out, B0, 1'b1);
  Full_Adder full_adder_5 (.A(A0), .B(xor_5_out), .C(1'b1), .S(S0), .C_2(full_adder_5_c_2));

  // Notes on the sheet:
  //   16
  //   If 1 then Positive
  //   8
  //   4
  //   2
  //   1
  //   1 to subtract and 0 to add
endmodule

// FD
module First_Decoder (
  input  C4,
  input  S3,
  input  S2,
  input  S1,
  input  S0,
  output a,
  output b,
  output c,
  output d,
  output e,
  output f,
  output g
);

  wire and_1_out, and_2_out, and_3_out, and_4_out, and_5_out, and_6_out, and_7_out, and_8_out, and_9_out,
       and_10_out, and_11_out, and_12_out, and_13_out, and_14_out, and_15_out, and_16_out, and_17_out,
       and_18_out, and_19_out, and_20_out, and_21_out, and_22_out, and_23_out, and_24_out, and_25_out,
       and_26_out, and_27_out, and_28_out, and_29_out, and_30_out, and_31_out, and_32_out, and_33_out,
       and_34_out, and_35_out, and_36_out, and_37_out, and_38_out, and_39_out, and_40_out, and_41_out,
       and_42_out, and_43_out, and_44_out, and_45_out, and_46_out, and_47_out, and_48_out, and_49_out,
       and_50_out, and_51_out, and_52_out, and_53_out, not_1_out, not_2_out, not_3_out, not_4_out, not_5_out,
       not_6_out, not_7_out, not_8_out, not_9_out, not_10_out, not_11_out, not_12_out, not_13_out,
       not_14_out, not_15_out, not_16_out, not_17_out, not_18_out, not_19_out, not_20_out, not_21_out,
       not_22_out, not_23_out, not_24_out, not_25_out, not_26_out, not_27_out, not_28_out, not_29_out,
       not_30_out, not_31_out, not_32_out, not_33_out, not_34_out, not_35_out, not_36_out, not_37_out,
       not_38_out, not_39_out, not_40_out, not_41_out, not_42_out, not_43_out, not_44_out, not_45_out,
       not_46_out, not_47_out, not_48_out, not_49_out, not_50_out, not_51_out, not_52_out, not_53_out,
       not_54_out, not_55_out, not_56_out, not_57_out, not_58_out, not_59_out, not_60_out, not_61_out,
       not_62_out, not_63_out, not_64_out, not_65_out, not_66_out, not_67_out, not_68_out, not_69_out,
       not_70_out, not_71_out, not_72_out, not_73_out, not_74_out, not_75_out, not_76_out, not_77_out,
       not_78_out, not_79_out, not_80_out, not_81_out, not_82_out, not_83_out, not_84_out;

  not not_1 (not_1_out, S3);
  not not_2 (not_2_out, S2);
  not not_3 (not_3_out, S0);
  not not_4 (not_4_out, C4);
  not not_5 (not_5_out, C4);
  not not_6 (not_6_out, S1);
  not not_7 (not_7_out, S1);
  not not_8 (not_8_out, S3);
  not not_9 (not_9_out, S2);
  not not_10 (not_10_out, S2);
  not not_11 (not_11_out, S0);
  not not_12 (not_12_out, S3);
  not not_13 (not_13_out, S2);
  not not_14 (not_14_out, S3);
  not not_15 (not_15_out, S2);
  not not_16 (not_16_out, S3);
  not not_17 (not_17_out, S2);
  not not_18 (not_18_out, S1);
  not not_19 (not_19_out, S0);
  not not_20 (not_20_out, C4);
  not not_21 (not_21_out, S2);
  not not_22 (not_22_out, C4);
  not not_23 (not_23_out, S1);
  not not_24 (not_24_out, C4);
  not not_25 (not_25_out, S0);
  not not_26 (not_26_out, S1);
  not not_27 (not_27_out, S0);
  not not_28 (not_28_out, C4);
  not not_29 (not_29_out, S3);
  not not_30 (not_30_out, S2);
  not not_31 (not_31_out, S2);
  not not_32 (not_32_out, S1);
  not not_33 (not_33_out, S3);
  not not_34 (not_34_out, S2);
  not not_35 (not_35_out, S3);
  not not_36 (not_36_out, S0);
  not not_37 (not_37_out, S2);
  not not_38 (not_38_out, S0);
  not not_39 (not_39_out, C4);
  not not_40 (not_40_out, S1);
  not not_41 (not_41_out, C4);
  not not_42 (not_42_out, S1);
  not not_43 (not_43_out, S1);
  not not_44 (not_44_out, C4);
  not not_45 (not_45_out, S3);
  not not_46 (not_46_out, S0);
  not not_47 (not_47_out, S3);
  not not_48 (not_48_out, S0);
  not not_49 (not_49_out, S3);
  not not_50 (not_50_out, S0);
  not not_51 (not_51_out, S2);
  not not_52 (not_52_out, S0);
  not not_53 (not_53_out, C4);
  not not_54 (not_54_out, S1);
  not not_55 (not_55_out, S0);
  not not_56 (not_56_out, S3);
  not not_57 (not_57_out, S0);
  not not_58 (not_58_out, S0);
  not not_59 (not_59_out, C4);
  not not_60 (not_60_out, S3);
  not not_61 (not_61_out, S1);
  not not_62 (not_62_out, C4);
  not not_63 (not_63_out, S3);
  not not_64 (not_64_out, S0);
  not not_65 (not_65_out, S2);
  not not_66 (not_66_out, S1);
  not not_67 (not_67_out, S0);
  not not_68 (not_68_out, C4);
  not not_69 (not_69_out, S1);
  not not_70 (not_70_out, S0);
  not not_71 (not_71_out, S3);
  not not_72 (not_72_out, S2);
  not not_73 (not_73_out, S1);
  not not_74 (not_74_out, S3);
  not not_75 (not_75_out, S2);
  not not_76 (not_76_out, S3);
  not not_77 (not_77_out, S0);
  not not_78 (not_78_out, C4);
  not not_79 (not_79_out, S1);
  not not_80 (not_80_out, S1);
  not not_81 (not_81_out, C4);
  not not_82 (not_82_out, S2);
  not not_83 (not_83_out, S0);
  not not_84 (not_84_out, S3);
  and and_1 (and_1_out, not_1_out, S1);
  and and_2 (and_2_out, not_2_out, S1, not_3_out);
  and and_3 (and_3_out, not_4_out, S2, S0);
  and and_4 (and_4_out, not_5_out, S3, not_6_out);
  and and_5 (and_5_out, S3, S2, not_7_out);
  and and_6 (and_6_out, C4, not_8_out, not_9_out);
  and and_7 (and_7_out, C4, not_10_out, S0);
  and and_8 (and_8_out, C4, S2, not_11_out);
  and and_9 (and_9_out, not_12_out, not_13_out, S0);
  and and_10 (and_10_out, not_14_out, not_15_out, S1);
  and and_11 (and_11_out, not_16_out, S1, S0);
  and and_12 (and_12_out, not_17_out, S1, S0);
  and and_13 (and_13_out, S2, not_18_out, not_19_out);
  and and_14 (and_14_out, not_20_out, S3, not_21_out);
  and and_15 (and_15_out, not_22_out, S3, not_23_out);
  and and_16 (and_16_out, not_24_out, S3, not_25_out);
  and and_17 (and_17_out, S3, not_26_out, not_27_out);
  and and_18 (and_18_out, C4, S2);
  and and_19 (and_19_out, not_28_out, not_29_out, S2);
  and and_20 (and_20_out, S3, not_30_out);
  and and_21 (and_21_out, S3, S1);
  and and_22 (and_22_out, C4, not_31_out);
  and and_23 (and_23_out, C4, not_32_out);
  and and_24 (and_24_out, not_33_out, not_34_out, S1);
  and and_25 (and_25_out, not_35_out, S1, not_36_out);
  and and_26 (and_26_out, not_37_out, S1, not_38_out);
  and and_27 (and_27_out, not_39_out, S2, not_40_out, S0);
  and and_28 (and_28_out, not_41_out, S3, not_42_out);
  and and_29 (and_29_out, S3, not_43_out, S0);
  and and_30 (and_30_out, not_44_out, S3, S2, S0);
  and and_31 (and_31_out, C4, not_45_out, not_46_out);
  and and_32 (and_32_out, C4, not_47_out, S1);
  and and_33 (and_33_out, C4, S2, not_48_out);
  and and_34 (and_34_out, not_49_out, S1, not_50_out);
  and and_35 (and_35_out, not_51_out, S1, not_52_out);
  and and_36 (and_36_out, not_53_out, S3, not_54_out, not_55_out);
  and and_37 (and_37_out, C4, not_56_out, not_57_out);
  and and_38 (and_38_out, C4, S2, not_58_out);
  and and_39 (and_39_out, not_59_out, not_60_out, S2, not_61_out);
  and and_40 (and_40_out, not_62_out, not_63_out, S2, not_64_out);
  and and_41 (and_41_out, S3, not_65_out, not_66_out);
  and and_42 (and_42_out, S3, S1, not_67_out);
  and and_43 (and_43_out, not_68_out, S3, S2, S1);
  and and_44 (and_44_out, C4, not_69_out, not_70_out);
  and and_45 (and_45_out, C4, not_71_out, not_72_out, S1);
  and and_46 (and_46_out, C4, S3, not_73_out);
  and and_47 (and_47_out, not_74_out, not_75_out, S1);
  and and_48 (and_48_out, not_76_out, S1, not_77_out);
  and and_49 (and_49_out, not_78_out, S2, not_79_out);
  and and_50 (and_50_out, S3, not_80_out);
  and and_51 (and_51_out, not_81_out, S3, S2);
  and and_52 (and_52_out, C4, not_82_out, not_83_out);
  and and_53 (and_53_out, C4, not_84_out, S1);
  or or_1 (a, and_1_out, and_2_out, and_3_out, and_4_out, and_5_out, and_6_out, and_7_out, and_8_out);
  or or_2 (b, and_9_out, and_10_out, and_11_out, and_12_out, and_13_out, and_14_out, and_15_out, and_16_out, and_17_out, and_18_out);
  or or_3 (c, S0, and_19_out, and_20_out, and_21_out, and_22_out, and_23_out);
  or or_4 (d, and_24_out, and_25_out, and_26_out, and_27_out, and_28_out, and_29_out, and_30_out, and_31_out, and_32_out, and_33_out);
  or or_5 (e, and_34_out, and_35_out, and_36_out, and_37_out, and_38_out);
  or or_6 (f, and_39_out, and_40_out, and_41_out, and_42_out, and_43_out, and_44_out, and_45_out, and_46_out);
  or or_7 (g, and_47_out, and_48_out, and_49_out, and_50_out, and_51_out, and_52_out, and_53_out);
endmodule

// SD
module Second_Decoder (
  input  C4,
  input  S3,
  input  S2,
  input  S1,
  input  S0,
  output a,
  output b,
  output c,
  output d,
  output e,
  output f,
  output g
);

  wire and_1_out, and_2_out, and_3_out, and_4_out, and_5_out, and_6_out, and_7_out, and_8_out, and_9_out,
       and_10_out, and_11_out, and_12_out, and_13_out, and_14_out, and_15_out, and_16_out, and_17_out,
       and_18_out, and_19_out, and_20_out, and_21_out, and_22_out, and_23_out, and_24_out, and_25_out,
       and_26_out, and_27_out, and_28_out, not_1_out, not_2_out, not_3_out, not_4_out, not_5_out, not_6_out,
       not_7_out, not_8_out, not_9_out, not_10_out, not_11_out, not_12_out, not_13_out, not_14_out,
       not_15_out, not_16_out, not_17_out, not_18_out, not_19_out, not_20_out, not_21_out, not_22_out,
       not_23_out, not_24_out, not_25_out, not_26_out, not_27_out, not_28_out, not_29_out, not_30_out,
       not_31_out, not_32_out, not_33_out, not_34_out, not_35_out, not_36_out, not_37_out, not_38_out;

  not not_1 (not_1_out, C4);
  not not_2 (not_2_out, S3);
  not not_3 (not_3_out, C4);
  not not_4 (not_4_out, S3);
  not not_5 (not_5_out, S3);
  not not_6 (not_6_out, S2);
  not not_7 (not_7_out, S1);
  or or_1 (b, S0, S1, S2, S3, C4);
  not not_8 (not_8_out, C4);
  not not_9 (not_9_out, C4);
  not not_10 (not_10_out, C4);
  not not_11 (not_11_out, C4);
  not not_12 (not_12_out, S3);
  not not_13 (not_13_out, S2);
  not not_14 (not_14_out, C4);
  not not_15 (not_15_out, S3);
  not not_16 (not_16_out, C4);
  not not_17 (not_17_out, S3);
  not not_18 (not_18_out, S3);
  not not_19 (not_19_out, S2);
  not not_20 (not_20_out, S1);
  not not_21 (not_21_out, C4);
  not not_22 (not_22_out, S3);
  not not_23 (not_23_out, C4);
  not not_24 (not_24_out, S3);
  not not_25 (not_25_out, S3);
  not not_26 (not_26_out, S2);
  not not_27 (not_27_out, S1);
  not not_28 (not_28_out, S2);
  not not_29 (not_29_out, S1);
  not not_30 (not_30_out, C4);
  not not_31 (not_31_out, S3);
  not not_32 (not_32_out, C4);
  not not_33 (not_33_out, S3);
  not not_34 (not_34_out, C4);
  not not_35 (not_35_out, S3);
  not not_36 (not_36_out, C4);
  not not_37 (not_37_out, S2);
  not not_38 (not_38_out, S1);
  and and_1 (and_1_out, C4, S2);
  and and_2 (and_2_out, C4, S3);
  and and_3 (and_3_out, not_1_out, not_2_out, S0);
  and and_4 (and_4_out, not_3_out, not_4_out, S1);
  and and_5 (and_5_out, not_5_out, S2);
  and and_6 (and_6_out, S3, not_6_out, not_7_out);
  and and_7 (and_7_out, C4, S3);
  and and_8 (and_8_out, not_8_out, S0);
  and and_9 (and_9_out, not_9_out, S1);
  and and_10 (and_10_out, not_10_out, S2);
  and and_11 (and_11_out, not_11_out, S3);
  and and_12 (and_12_out, S3, S2, S1);
  and and_13 (and_13_out, C4, not_12_out, not_13_out);
  and and_14 (and_14_out, not_14_out, not_15_out, S0);
  and and_15 (and_15_out, not_16_out, not_17_out, S1);
  and and_16 (and_16_out, not_18_out, S2);
  and and_17 (and_17_out, S3, not_19_out, not_20_out);
  and and_18 (and_18_out, C4, S3);
  and and_19 (and_19_out, not_21_out, not_22_out, S0);
  and and_20 (and_20_out, not_23_out, not_24_out, S1);
  and and_21 (and_21_out, not_25_out, S2);
  and and_22 (and_22_out, S3, not_26_out, not_27_out);
  and and_23 (and_23_out, C4, S3, not_28_out);
  and and_24 (and_24_out, C4, S3, not_29_out);
  and and_25 (and_25_out, not_30_out, not_31_out, S0);
  and and_26 (and_26_out, not_32_out, not_33_out, S1);
  and and_27 (and_27_out, not_34_out, not_35_out, S2);
  and and_28 (and_28_out, not_36_out, S3, not_37_out, not_38_out);
  or or_2 (g, and_1_out, and_2_out);
  or or_3 (a, and_3_out, and_4_out, and_5_out, and_6_out, and_7_out);
  or or_4 (c, and_8_out, and_9_out, and_10_out, and_11_out, and_12_out, and_13_out);
  or or_5 (d, and_14_out, and_15_out, and_16_out, and_17_out, and_18_out);
  or or_6 (e, and_19_out, and_20_out, and_21_out, and_22_out, and_23_out, and_24_out);
  or or_7 (f, and_25_out, and_26_out, and_27_out, and_28_out);
endmodule

module Display (
  input  in_1,
  input  [4:0] A,
  input  [4:0] B
);

  wire first_decoder_1_a, first_decoder_1_b, first_decoder_1_c, first_decoder_1_d, first_decoder_1_e,
       first_decoder_1_f, first_decoder_1_g, first_decoder_2_a, first_decoder_2_b, first_decoder_2_c,
       first_decoder_2_d, first_decoder_2_e, first_decoder_2_f, first_decoder_2_g, first_decoder_3_a,
       first_decoder_3_b, first_decoder_3_c, first_decoder_3_d, first_decoder_3_e, first_decoder_3_f,
       first_decoder_3_g, n5_bit_subtractor_1_c, not_1_out, second_decoder_1_a, second_decoder_1_b,
       second_decoder_1_c, second_decoder_1_d, second_decoder_1_e, second_decoder_1_f, second_decoder_1_g,
       second_decoder_2_a, second_decoder_2_b, second_decoder_2_c, second_decoder_2_d, second_decoder_2_e,
       second_decoder_2_f, second_decoder_2_g, second_decoder_3_a, second_decoder_3_b, second_decoder_3_c,
       second_decoder_3_d, second_decoder_3_e, second_decoder_3_f, second_decoder_3_g, switchn_1_z1,
       switchn_1_z2;
  wire [3:0] FD_2_a, FD_3_a, FD_a, SD_2_a, SD_3_a, SD_a;
  wire [4:0] _2_s_out, n5_bit_subtractor_1_s0, revert_1_out, revert_2_out, revert_3_out, Switch_z,
       switcht_1_z1, switcht_1_z2, switcht_2_z1, switcht_2_z2, switcht_3_z1, switcht_3_z2;

  Revert revert_1 (.In(B), .Out(revert_1_out));
  Revert revert_2 (.In(A), .Out(revert_2_out));
  Switch Switch (.A(n5_bit_subtractor_1_s0), .B(_2_s_out), .Switch(n5_bit_subtractor_1_c), .Z(Switch_z));
  _2_s_Compliment _2_s (.In(n5_bit_subtractor_1_s0), .Out(_2_s_out));
  _5_bit_Subtractor u_5_bit_subtractor_1 (
    .B4(B[4]), .A4(A[4]), .B3(B[3]), .A3(A[3]), .B2(B[2]), .A2(A[2]), .B1(B[1]), .A1(A[1]), .B0(B[0]),
    .A0(A[0]), .C(n5_bit_subtractor_1_c), .S4(n5_bit_subtractor_1_s0[4]), .S3(n5_bit_subtractor_1_s0[3]),
    .S2(n5_bit_subtractor_1_s0[2]), .S1(n5_bit_subtractor_1_s0[1]), .S0(n5_bit_subtractor_1_s0[0]));
  Revert revert_3 (.In(Switch_z), .Out(revert_3_out));
  SwitchT switcht_1 (.Switch(in_1), .B(revert_1_out), .Z1(switcht_1_z1), .Z2(switcht_1_z2));
  SwitchT switcht_2 (.Switch(in_1), .B(revert_2_out), .Z1(switcht_2_z1), .Z2(switcht_2_z2));
  _7_Segment_Display u_7_segment_display_1 (
    .g(second_decoder_1_g), .f(second_decoder_1_f), .a(second_decoder_1_a), .b(second_decoder_1_b),
    .e(second_decoder_1_e), .d(second_decoder_1_d), .c(second_decoder_1_c));  // open: dp
  Second_Decoder second_decoder_1 (
    .C4(switcht_2_z2[0]), .S3(switcht_2_z2[1]), .S2(switcht_2_z2[2]), .S1(switcht_2_z2[3]),
    .S0(switcht_2_z2[4]), .a(second_decoder_1_a), .b(second_decoder_1_b), .c(second_decoder_1_c),
    .d(second_decoder_1_d), .e(second_decoder_1_e), .f(second_decoder_1_f), .g(second_decoder_1_g));
  not not_1 (not_1_out, n5_bit_subtractor_1_c);
  Hex_Digit_Display hex_digit_display_1 (.value(SD_a));  // open: dp
  Second_Decoder__Hex SD (
    .C4(switcht_2_z1[0]), .S3(switcht_2_z1[1]), .S2(switcht_2_z1[2]), .S1(switcht_2_z1[3]),
    .S0(switcht_2_z1[4]), .a(SD_a[0]), .b(SD_a[1]), .c(SD_a[2]), .d(SD_a[3]));
  First_Decoder__Hex FD (
    .C4(switcht_2_z1[0]), .S3(switcht_2_z1[1]), .S2(switcht_2_z1[2]), .S1(switcht_2_z1[3]),
    .S0(switcht_2_z1[4]), .a(FD_a[0]), .b(FD_a[1]), .c(FD_a[2]), .d(FD_a[3]));
  _7_Segment_Display u_7_segment_display_2 (
    .g(first_decoder_1_g), .f(first_decoder_1_f), .a(first_decoder_1_a), .b(first_decoder_1_b),
    .e(first_decoder_1_e), .d(first_decoder_1_d), .c(first_decoder_1_c));  // open: dp
  First_Decoder first_decoder_1 (
    .C4(switcht_2_z2[0]), .S3(switcht_2_z2[1]), .S2(switcht_2_z2[2]), .S1(switcht_2_z2[3]),
    .S0(switcht_2_z2[4]), .a(first_decoder_1_a), .b(first_decoder_1_b), .c(first_decoder_1_c),
    .d(first_decoder_1_d), .e(first_decoder_1_e), .f(first_decoder_1_f), .g(first_decoder_1_g));
  Hex_Digit_Display hex_digit_display_2 (.value(FD_a));  // open: dp
  Second_Decoder__Hex SD_2 (
    .C4(switcht_1_z1[0]), .S3(switcht_1_z1[1]), .S2(switcht_1_z1[2]), .S1(switcht_1_z1[3]),
    .S0(switcht_1_z1[4]), .a(SD_2_a[0]), .b(SD_2_a[1]), .c(SD_2_a[2]), .d(SD_2_a[3]));
  _7_Segment_Display u_7_segment_display_3 (
    .g(second_decoder_2_g), .f(second_decoder_2_f), .a(second_decoder_2_a), .b(second_decoder_2_b),
    .e(second_decoder_2_e), .d(second_decoder_2_d), .c(second_decoder_2_c));  // open: dp
  Second_Decoder second_decoder_2 (
    .C4(switcht_1_z2[0]), .S3(switcht_1_z2[1]), .S2(switcht_1_z2[2]), .S1(switcht_1_z2[3]),
    .S0(switcht_1_z2[4]), .a(second_decoder_2_a), .b(second_decoder_2_b), .c(second_decoder_2_c),
    .d(second_decoder_2_d), .e(second_decoder_2_e), .f(second_decoder_2_f), .g(second_decoder_2_g));
  SwitchN switchn_1 (.Switch(in_1), .B(not_1_out), .Z1(switchn_1_z1), .Z2(switchn_1_z2));
  Hex_Digit_Display hex_digit_display_3 (.value(SD_2_a));  // open: dp
  Hex_Digit_Display hex_digit_display_4 (.value(FD_2_a));  // open: dp
  First_Decoder__Hex FD_2 (
    .C4(switcht_1_z1[0]), .S3(switcht_1_z1[1]), .S2(switcht_1_z1[2]), .S1(switcht_1_z1[3]),
    .S0(switcht_1_z1[4]), .a(FD_2_a[0]), .b(FD_2_a[1]), .c(FD_2_a[2]), .d(FD_2_a[3]));
  _7_Segment_Display u_7_segment_display_4 (
    .g(first_decoder_2_g), .f(first_decoder_2_f), .a(first_decoder_2_a), .b(first_decoder_2_b),
    .e(first_decoder_2_e), .d(first_decoder_2_d), .c(first_decoder_2_c));  // open: dp
  First_Decoder first_decoder_2 (
    .C4(switcht_1_z2[0]), .S3(switcht_1_z2[1]), .S2(switcht_1_z2[2]), .S1(switcht_1_z2[3]),
    .S0(switcht_1_z2[4]), .a(first_decoder_2_a), .b(first_decoder_2_b), .c(first_decoder_2_c),
    .d(first_decoder_2_d), .e(first_decoder_2_e), .f(first_decoder_2_f), .g(first_decoder_2_g));
  SwitchT switcht_3 (.Switch(in_1), .B(revert_3_out), .Z1(switcht_3_z1), .Z2(switcht_3_z2));
  _7_Segment_Display u_7_segment_display_5 (
    .g(second_decoder_3_g), .f(second_decoder_3_f), .a(second_decoder_3_a), .b(second_decoder_3_b),
    .e(second_decoder_3_e), .d(second_decoder_3_d), .c(second_decoder_3_c));  // open: dp
  _7_Segment_Display u_7_segment_display_6 (.g(switchn_1_z2));  // open: f, a, b, e, d, c, dp
  Second_Decoder second_decoder_3 (
    .C4(switcht_3_z2[0]), .S3(switcht_3_z2[1]), .S2(switcht_3_z2[2]), .S1(switcht_3_z2[3]),
    .S0(switcht_3_z2[4]), .a(second_decoder_3_a), .b(second_decoder_3_b), .c(second_decoder_3_c),
    .d(second_decoder_3_d), .e(second_decoder_3_e), .f(second_decoder_3_f), .g(second_decoder_3_g));
  _7_Segment_Display u_7_segment_display_7 (.g(switchn_1_z1));  // open: f, a, b, e, d, c, dp
  Second_Decoder__Hex SD_3 (
    .C4(switcht_3_z1[0]), .S3(switcht_3_z1[1]), .S2(switcht_3_z1[2]), .S1(switcht_3_z1[3]),
    .S0(switcht_3_z1[4]), .a(SD_3_a[0]), .b(SD_3_a[1]), .c(SD_3_a[2]), .d(SD_3_a[3]));
  _7_Segment_Display u_7_segment_display_8 (
    .g(first_decoder_3_g), .f(first_decoder_3_f), .a(first_decoder_3_a), .b(first_decoder_3_b),
    .e(first_decoder_3_e), .d(first_decoder_3_d), .c(first_decoder_3_c));  // open: dp
  Hex_Digit_Display hex_digit_display_5 (.value(SD_3_a));  // open: dp
  Hex_Digit_Display hex_digit_display_6 (.value(FD_3_a));  // open: dp
  First_Decoder__Hex FD_3 (
    .C4(switcht_3_z1[0]), .S3(switcht_3_z1[1]), .S2(switcht_3_z1[2]), .S1(switcht_3_z1[3]),
    .S0(switcht_3_z1[4]), .a(FD_3_a[0]), .b(FD_3_a[1]), .c(FD_3_a[2]), .d(FD_3_a[3]));
  First_Decoder first_decoder_3 (
    .C4(switcht_3_z2[0]), .S3(switcht_3_z2[1]), .S2(switcht_3_z2[2]), .S1(switcht_3_z2[3]),
    .S0(switcht_3_z2[4]), .a(first_decoder_3_a), .b(first_decoder_3_b), .c(first_decoder_3_c),
    .d(first_decoder_3_d), .e(first_decoder_3_e), .f(first_decoder_3_f), .g(first_decoder_3_g));

  // Notes on the sheet:
  //   Switch from Binary to Hexa
  //   If equals 1 positive else negative
  //   -
  //   -
  //   =
  //   =
endmodule

module Switch (
  input  Switch,
  input  [4:0] A,
  input  [4:0] B,
  output [4:0] Z
);

  wire and_1_out, and_2_out, and_3_out, and_4_out, and_5_out, and_6_out, and_7_out, and_8_out, and_9_out,
       and_10_out, not_1_out;

  and and_1 (and_1_out, A[4], Switch);
  and and_2 (and_2_out, A[3], Switch);
  and and_3 (and_3_out, A[2], Switch);
  and and_4 (and_4_out, A[1], Switch);
  or or_1 (Z[4], and_1_out, and_6_out);
  and and_5 (and_5_out, A[0], Switch);
  or or_2 (Z[3], and_2_out, and_7_out);
  not not_1 (not_1_out, Switch);
  or or_3 (Z[2], and_3_out, and_8_out);
  or or_4 (Z[1], and_4_out, and_9_out);
  or or_5 (Z[0], and_5_out, and_10_out);
  and and_6 (and_6_out, B[4], not_1_out);
  and and_7 (and_7_out, B[3], not_1_out);
  and and_8 (and_8_out, B[2], not_1_out);
  and and_9 (and_9_out, B[1], not_1_out);
  and and_10 (and_10_out, B[0], not_1_out);
endmodule

module Revert (
  input  [4:0] In,
  output [4:0] Out
);


  assign Out = {In[0], In[1], In[2], In[3], In[4]};
endmodule

module First_Decoder__Hex (
  input  C4,
  input  S3,
  input  S2,
  input  S1,
  input  S0,
  output a,
  output b,
  output c,
  output d
);


  assign a = S0;
  assign b = S1;
  assign c = S2;
  assign d = S3;
endmodule

module Second_Decoder__Hex (
  input  C4,
  input  S3,
  input  S2,
  input  S1,
  input  S0,
  output a,
  output b,
  output c,
  output d
);


  assign a = C4;
  assign b = 1'b0;
  assign c = 1'b0;
  assign d = 1'b0;
endmodule

module SwitchT (
  input  Switch,
  input  [4:0] B,
  output [4:0] Z2,
  output [4:0] Z1
);

  wire not_1_out;

  and and_1 (Z1[4], B[4], Switch);
  and and_2 (Z1[2], B[2], Switch);
  and and_3 (Z1[3], B[3], Switch);
  and and_4 (Z1[1], B[1], Switch);
  and and_5 (Z1[0], B[0], Switch);
  not not_1 (not_1_out, Switch);
  and and_6 (Z2[4], B[4], not_1_out);
  and and_7 (Z2[3], B[3], not_1_out);
  and and_8 (Z2[2], B[2], not_1_out);
  and and_9 (Z2[1], B[1], not_1_out);
  and and_10 (Z2[0], B[0], not_1_out);
endmodule

module SwitchN (
  input  Switch,
  input  B,
  output Z2,
  output Z1
);

  wire not_1_out;

  and and_1 (Z1, B, Switch);
  not not_1 (not_1_out, Switch);
  and and_2 (Z2, B, not_1_out);
endmodule
